# Fritzing sketch project-3-diagram (saved by Fritzing 0.9.3b)
breadboards: 1

parts:
  LED1 = LED - 5mm [color="Red (633nm)" package="5 mm [THT]"]
  Part1 = Arduino Uno (Rev3)
  R1 = Rotary Potentiometer (Small) [maximum_resistance=100kΩ package=THT]
  R2 = Resistor [tolerance=±5% resistance=220 package=THT]

nets:
  N1: LED1.cathode, R2.Pin_0
  N2: LED1.anode, Part1.D3_PWM
  N3: Part1.A0, R1.wiper
  N4: Part1.5V, R1.leg2
  N5: Part1.GND, R1.leg1, R2.Pin_1
