# Fritzing sketch binary_breadboard (saved by Fritzing 0.9.3b)
breadboards: 1

parts:
  Part1 = Arduino Uno (Rev3)
  S1 = Pushbutton [package="[THT]"]
  S2 = Pushbutton [package="[THT]"]
  S3 = Pushbutton [package="[THT]"]
  R1 = Resistor [tolerance=±5% resistance=220 package=THT]
  R2 = Resistor [tolerance=±5% resistance=220 package=THT]
  R3 = Resistor [tolerance=±5% resistance=220 package=THT]
  R4 = Resistor [tolerance=±5% resistance=220 package=THT]
  R5 = Resistor [tolerance=±5% resistance=220 package=THT]
  R6 = Resistor [tolerance=±5% resistance=220 package=THT]
  R7 = Resistor [tolerance=±5% resistance=220 package=THT]
  LED1 = LED - 5mm [color="Red (633nm)" package="5 mm [THT]"]
  LED2 = LED - 5mm [color="Red (633nm)" package="5 mm [THT]"]
  LED3 = LED - 5mm [color="Red (633nm)" package="5 mm [THT]"]
  LED4 = LED - 5mm [color="Red (633nm)" package="5 mm [THT]"]
  LED5 = LED - 5mm [color="Red (633nm)" package="5 mm [THT]"]
  LED6 = LED - 5mm [color="Red (633nm)" package="5 mm [THT]"]
  LED7 = LED - 5mm [color="Red (633nm)" package="5 mm [THT]"]
  R8 = Resistor [tolerance=±5% resistance=10k package=THT]
  R9 = Resistor [tolerance=±5% resistance=10k package=THT]
  R10 = Resistor [tolerance=±5% resistance=10k package=THT]

nets:
  N1: Part1.D8, LED7.anode
  N2: Part1.D10_PWM/SS, S1.Pin_1, S1.Pin_2, R9.Pin_0
  N3: Part1.D11_PWM/MOSI, S2.Pin_1, S2.Pin_2, R10.Pin_0
  N4: Part1.D12/MISO, S3.Pin_1, S3.Pin_2, R8.Pin_0
  N5: Part1.D2, LED1.anode
  N6: Part1.D3_PWM, LED2.anode
  N7: Part1.D4, LED3.anode
  N8: Part1.D5_PWM, LED4.anode
  N9: Part1.D6_PWM, LED5.anode
  N10: Part1.D7, LED6.anode
  N11: Part1.5V, S1.Pin_3, S1.Pin_4, S2.Pin_3, S2.Pin_4, S3.Pin_3, S3.Pin_4
  N12: Part1.GND, R1.Pin_1, R2.Pin_1, R3.Pin_1, R4.Pin_1, R5.Pin_1, R6.Pin_1, R7.Pin_1, R8.Pin_1, R9.Pin_1, R10.Pin_1
  N13: R1.Pin_0, LED5.cathode
  N14: R2.Pin_0, LED7.cathode
  N15: R3.Pin_0, LED6.cathode
  N16: R4.Pin_0, LED4.cathode
  N17: R5.Pin_0, LED3.cathode
  N18: R6.Pin_0, LED2.cathode
  N19: R7.Pin_0, LED1.cathode
